# Fritzing sketch dimmer (saved by Fritzing 0.9.3b)
circuit board: 9.9cm x 4cm
breadboards: 1

parts:
  R1 = Resistor [tolerance=±5% resistance=33k power=2W package=THT]
  A/C_IN = Screw terminal - 2 pins [package=THT]
  R2 = Resistor [tolerance=±5% resistance=33k power=2W package=THT]
  HLK-PM1 = HLK-PM01
  A/C_OUT = Screw terminal - 2 pins [package=THT]
  ATTINY85 = ATTINY45 [package=dip]
  R3 = Resistor [tolerance=±5% resistance=10k package=THT]
  R4 = Resistor [tolerance=±5% resistance=10k package=THT]
  IL251 = IC, DIP package, 6 pins [chip_label=IL251]
  U2 = ESP8266-12e_smt [part_number=ESP8266-12E]
  R5 = Resistor [tolerance=±5% resistance=220 package=THT]
  C1 = Film/Foil Capacitor [capacitance=100nF voltage=35V package="15mm [THT, pp]"]
  R6 = Resistor [tolerance=±5% resistance=220 package=THT]
  R7 = Resistor [tolerance=±5% resistance=220 package=THT]
  TRI1 = BTA Triac [package="TO220 [THT]"]
  MOC3021 = IC, DIP package, 6 pins [chip_label=MOC3201]
  R8 = Resistor [tolerance=±5% resistance=10k package=THT]
  IC1 = Voltage Regulator [package=to-92]
  R9 = Resistor [tolerance=±5% resistance=10k package=THT]
  R10 = Resistor [tolerance=±5% resistance=10k package=THT]
  S1 = Momentary Switch [package=ksa_sealed_tac_switch]
  2A = Fuse with Handler [part_number=Htc-15m]
  J2 = female pin header, 4 pins [form="♀ (female)"]

nets:
  N1: R1.Pin_0, A/C_IN.pin2, HLK-PM1.AC#1, A/C_OUT.pin1, C1.-, R6.Pin_0, R6.Pin_1
  N2: R1.Pin_1, IL251.pin1
  N3: A/C_IN.pin1, 2A.Connector1
  N4: R2.Pin_0, HLK-PM1.AC#0, R7.Pin_0, TRI1.A2, 2A.Connector2
  N5: R2.Pin_1, IL251.pin2
  GND: HLK-PM1.-Vo, ATTINY85.GND, IL251.pin4, U2.GND, MOC3021.pin2, R8.Pin_0, IC1.GND, S1.1, J2.pin4
  N6: HLK-PM1.+Vo, ATTINY85.VCC, R3.Pin_1, R4.Pin_0, IC1.IN
  N7: A/C_OUT.pin2, C1.+, TRI1.A1
  N8: ATTINY85.PB5(NRES), R4.Pin_1, U2.GPIO_16
  N9: ATTINY85.PB3(ADC3), R5.Pin_0
  N10: ATTINY85.PB4(ADC2), R3.Pin_0, IL251.pin5
  N11: ATTINY85.PB0(MOSI), U2.GPIO_4
  N12: ATTINY85.PB2(SCK_ADC1), U2.GPIO_5
  N13: U2.REST, R10.Pin_1
  N14: U2.CH_PD, R9.Pin_1
  N15: U2.VCC, IC1.OUT, R9.Pin_0, R10.Pin_0, J2.pin1
  N16: U2.GPIO_15, R8.Pin_1
  N17: U2.GPIO_0, S1.3
  N18: U2.GPIO_3/RXD, J2.pin2
  N19: U2.GPIO_1/TXD, J2.pin3
  N20: R5.Pin_1, MOC3021.pin1
  N21: R7.Pin_1, MOC3021.pin6
  N22: TRI1.G, MOC3021.pin4

notes:
  L
  N

custom parts:
  HLK-PM01: AC-DC 220V to 5V Step-Down Power Supply Module
  ESP8266-12e_smt: These are the first series of modules made with the ESP8266 by the third-party manufacturer AI-Thinker and remain the most widely available. They are collectively referred to as "ESP-xx modules" and to form a workable development system require additional components, especially a serial TTL-to-USB adapter (sometimes called a USB-to-UART bridge) and an external 3.3V power supply. ESP8266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
  BTA Triac: BTA16
